// Logisim project add_sub.circ as structural Verilog: 4 circuits, main circuit main
module main (
  input  [3:0] Y,
  input  OP,
  input  [3:0] X,
  output [3:0] R
);

  wire fulladder_1_cn1, fulladder_2_cn1, fulladder_3_cn1, fulladder_4_cn1;
  wire [3:0] controlled_not_1_dataout;

  controlled_not controlled_not_1 (.DataIn(Y), .C(OP), .DataOut(controlled_not_1_dataout));
  FullAdder fulladder_1 (
    .Xn(X[1]), .Yn(controlled_not_1_dataout[1]), .Cn(fulladder_4_cn1), .Sn(R[1]), .Cn1(fulladder_1_cn1));
  FullAdder fulladder_2 (
    .Xn(X[2]), .Yn(controlled_not_1_dataout[2]), .Cn(fulladder_1_cn1), .Sn(R[2]), .Cn1(fulladder_2_cn1));
  FullAdder fulladder_3 (
    .Xn(X[3]), .Yn(controlled_not_1_dataout[3]), .Cn(fulladder_2_cn1), .Sn(R[3]), .Cn1(fulladder_3_cn1));
  FullAdder fulladder_4 (.Xn(X[0]), .Yn(controlled_not_1_dataout[0]), .Cn(OP), .Sn(R[0]), .Cn1(fulladder_4_cn1));

  // Notes on the sheet:
  //   OP = 0, R = X + Y
  //   OP = 1, R = X - Y
endmodule

module FullAdder (
  input  Xn,
  input  Yn,
  input  Cn,
  output Sn,
  output Cn1
);

  wire and_1_out, and_2_out, and_3_out, and_4_out, and_5_out, and_6_out, and_7_out, and_8_out;

  and and_1 (and_1_out, ~Xn, ~Yn, Cn);  // AND_Gate
  and and_2 (and_2_out, ~Xn, Yn, ~Cn);  // AND_Gate
  and and_3 (and_3_out, Xn, ~Yn, ~Cn);  // AND_Gate
  and and_4 (and_4_out, Xn, Yn, Cn);
  and and_5 (and_5_out, ~Xn, Yn, Cn);  // AND_Gate
  and and_6 (and_6_out, Xn, ~Yn, Cn);  // AND_Gate
  and and_7 (and_7_out, Xn, Yn, ~Cn);  // AND_Gate
  and and_8 (and_8_out, Xn, Yn, Cn);
  or or_1 (Sn, and_1_out, and_2_out, and_3_out, and_4_out);
  or or_2 (Cn1, and_5_out, and_6_out, and_7_out, and_8_out);
endmodule

module HalfAdder (
  input  X0,
  input  Y0,
  output S0,
  output C1
);

  xor xor_1 (S0, X0, Y0);
  and and_1 (C1, X0, Y0);
endmodule

module controlled_not (
  input  [3:0] DataIn,
  input  C,
  output [3:0] DataOut
);

  xor xor_1 (DataOut[0], DataIn[0], C);
  xor xor_2 (DataOut[1], DataIn[1], C);
  xor xor_3 (DataOut[2], DataIn[2], C);
  xor xor_4 (DataOut[3], C, DataIn[3]);
endmodule
