// Logisim project christmas_light.circ as structural Verilog: 1 circuit, main circuit main
module main (
);

  wire button_1_out, clock_1_out;
  wire [1:0] counter_1_q;
  wire [2:0] counter_2_q;
  wire [7:0] rom_1_data;

  Clock clock_1 (.out(clock_1_out));
  Counter #(.max('h2), .width(2)) counter_1 (
    .clk(button_1_out), .Q(counter_1_q));  // open: clr, load, up, count, D, carry
  Button button_1 (.out(button_1_out));
  Counter #(.max('h7), .width(3)) counter_2 (
    .clk(clock_1_out), .Q(counter_2_q));  // open: clr, load, up, count, D, carry
  ROM rom_1 (.addr({3'b000, counter_1_q, counter_2_q}), .data(rom_1_data));
  // Probe on {3'b000, counter_1_q, counter_2_q}
  LED led_1 (.in(rom_1_data[0]));
  LED led_2 (.in(rom_1_data[1]));
  LED led_3 (.in(rom_1_data[2]));
  LED led_4 (.in(rom_1_data[3]));
  LED led_5 (.in(rom_1_data[4]));
  LED led_6 (.in(rom_1_data[5]));
  LED led_7 (.in(rom_1_data[6]));
  LED led_8 (.in(rom_1_data[7]));

  // Notes on the sheet:
  //   contents of rom_1 (hex, n*v repeats v):
  //   1 2 4 8 10 20 40 80 3 6 c 18 30 60 c0 81 81 42 24 18 18 24 42 81
endmodule
