// Logisim project christmas_light_with_branch.circ as structural Verilog: 1 circuit, main circuit main
module main (
);

  wire and_1_out, and_2_out, and_3_out, and_4_out, and_5_out, and_6_out, and_7_out, and_8_out, clock_1_out;
  wire [7:0] counter_1_q, new_value;
  wire [8:8] rom_1_data;

  Clock clock_1 (.out(clock_1_out));
  Counter counter_1 (
    .load(rom_1_data[8]), .clk(clock_1_out), .D(new_value), .Q(counter_1_q));  // open: clr, up, count, carry
  ROM #(.dataWidth(9)) rom_1 (.addr(counter_1_q), .data({rom_1_data[8], new_value}));
  // Probe on counter_1_q
  and and_1 (and_1_out, new_value[0], ~rom_1_data[8]);  // AND_Gate
  and and_2 (and_2_out, new_value[1], ~rom_1_data[8]);  // AND_Gate
  and and_3 (and_3_out, new_value[2], ~rom_1_data[8]);  // AND_Gate
  and and_4 (and_4_out, new_value[3], ~rom_1_data[8]);  // AND_Gate
  and and_5 (and_5_out, new_value[4], ~rom_1_data[8]);  // AND_Gate
  and and_6 (and_6_out, new_value[5], ~rom_1_data[8]);  // AND_Gate
  and and_7 (and_7_out, new_value[6], ~rom_1_data[8]);  // AND_Gate
  and and_8 (and_8_out, new_value[7], ~rom_1_data[8]);  // AND_Gate
  LED led_1 (.in(and_1_out));
  LED led_2 (.in(and_2_out));
  LED led_3 (.in(and_3_out));
  LED led_4 (.in(and_4_out));
  LED led_5 (.in(and_5_out));
  LED led_6 (.in(and_6_out));
  LED led_7 (.in(and_7_out));
  LED led_8 (.in(and_8_out));

  // Notes on the sheet:
  //   contents of rom_1 (hex, n*v repeats v):
  //   1 2 4 8 10 20 40 80 100 0 ff 109 80 40 20 10 8 4 2 1 10c f f0 115
endmodule
