// Logisim project ff_t.circ as structural Verilog: 1 circuit, main circuit main
module main (
  input  in_1,
  input  in_2,
  output out_3,
  output out_4
);

  wire d_ff_1_qn;

  D_Flip_Flop d_ff_1 (.D(d_ff_1_qn), .clk(in_1), .Q(out_3), .Qn(d_ff_1_qn));  // open: preset, reset
  T_Flip_Flop t_ff_1 (.T(1'b1), .clk(in_2), .Q(out_4));  // open: Qn, reset, preset
endmodule
