// Logisim project flip_flop_d.circ as structural Verilog: 1 circuit, main circuit main
module main (
  input  D,
  input  CLOCK,
  output Q,
  output nQ
);

  wire nand_1_out, nand_2_out, not_1_out;

  not not_1 (not_1_out, D);
  nand nand_1 (nand_1_out, D, CLOCK);
  nand nand_2 (nand_2_out, CLOCK, not_1_out);
  nand nand_3 (Q, nand_1_out, nQ);
  nand nand_4 (nQ, Q, nand_2_out);

  // Notes on the sheet:
  //   CLOCK: initial=0x1
  //   D: initial=0x1
endmodule
