// Logisim project led_sequence_with_rom_and_mux.circ as structural Verilog: 3 circuits, main circuit main
module main (
  input  [1:0] N_SEQ,
  input  in_2
);

  wire clock_1_out, contatore_1_b3, contatore_1_b4;
  wire [4:0] contatore_1_b0;
  wire [7:0] rom_1_data;

  Clock clock_1 (.out(clock_1_out));
  contatore contatore_1 (
    .CLK(clock_1_out), .b4(contatore_1_b4), .b3(contatore_1_b3), .b2(contatore_1_b0[2]),
    .b1(contatore_1_b0[1]), .b0(contatore_1_b0[0]));
  ROM #(.addrWidth(5)) rom_1 (.addr(contatore_1_b0), .data(rom_1_data));
  multiplex_2_1 multiplex_2_1_1 (.x0(N_SEQ[1]), .x1(contatore_1_b4), .c(in_2), .y(contatore_1_b0[4]));
  multiplex_2_1 multiplex_2_1_2 (.x0(N_SEQ[0]), .x1(contatore_1_b3), .c(in_2), .y(contatore_1_b0[3]));
  LED led_1 (.in(rom_1_data[0]));
  LED led_2 (.in(rom_1_data[1]));
  LED led_3 (.in(rom_1_data[2]));
  LED led_4 (.in(rom_1_data[3]));
  LED led_5 (.in(rom_1_data[4]));
  LED led_6 (.in(rom_1_data[5]));
  LED led_7 (.in(rom_1_data[6]));
  LED led_8 (.in(rom_1_data[7]));

  // Notes on the sheet:
  //   contents of rom_1 (hex, n*v repeats v):
  //   1 2 4 8 10 20 40 80 3 6 c 18 30 60 c0 80 81 42 24 18 18 24 42 81 80 40 20 10 8 4 2 1
endmodule

module contatore (
  input  CLK,
  output b4,
  output b3,
  output b2,
  output b1,
  output b0
);

  T_Flip_Flop #(.trigger("falling")) t_ff_1 (.T(1'b1), .clk(CLK), .Q(b0));  // open: Qn, reset, preset
  T_Flip_Flop #(.trigger("falling")) t_ff_2 (.T(1'b1), .clk(b0), .Q(b1));  // open: Qn, reset, preset
  T_Flip_Flop #(.trigger("falling")) t_ff_3 (.T(1'b1), .clk(b1), .Q(b2));  // open: Qn, reset, preset
  T_Flip_Flop #(.trigger("falling")) t_ff_4 (.T(1'b1), .clk(b2), .Q(b3));  // open: Qn, reset, preset
  T_Flip_Flop #(.trigger("falling")) t_ff_5 (.T(1'b1), .clk(b3), .Q(b4));  // open: Qn, reset, preset
endmodule

module multiplex_2_1 (
  input  x0,
  input  x1,
  input  c,
  output y
);

  wire and_1_out, and_2_out;

  and and_1 (and_1_out, x0, ~c);  // AND_Gate
  and and_2 (and_2_out, x1, c);
  or or_1 (y, and_1_out, and_2_out);
endmodule
