// Logisim project less_than_10.circ as structural Verilog: 1 circuit, main circuit main
module main (
  input  [3:0] A,
  output Less_Than_10
);

  wire and_1_out;

  and and_1 (and_1_out, ~A[1], ~A[2], A[3]);  // AND_Gate
  or or_1 (Less_Than_10, and_1_out, ~A[3]);  // OR_Gate
endmodule
