// Logisim project priority_encoder.circ as structural Verilog: 1 circuit, main circuit main
module main (
  input  X0,
  input  X1,
  input  X2,
  input  X3,
  output [1:0] out_5,
  output y1,
  output y0,
  output Invalid
);

  wire and_2_out, and_3_out;

  and and_1 (out_5[1], ~X0, ~X1);  // AND_Gate
  and and_2 (and_2_out, ~X0, X1, X2);  // AND_Gate
  and and_3 (and_3_out, ~X0, ~X2);  // AND_Gate
  or or_1 (out_5[0], and_2_out, and_3_out);
  and and_4 (Invalid, ~X0, ~X1, ~X2, ~X3);  // AND_Gate

  assign y0 = out_5[0];
  assign y1 = out_5[1];
endmodule
