// Logisim project shift_register.circ as structural Verilog: 1 circuit, main circuit main
module main (
  input  [3:0] in_1,
  input  LOAD,
  input  in_3,
  output [3:0] out_4
);

  wire multiplexer_1_out, multiplexer_2_out, multiplexer_3_out, multiplexer_4_out;

  Multiplexer multiplexer_1 (.in0(1'b0), .in1(in_1[0]), .out(multiplexer_1_out), .sel(LOAD));
  Multiplexer multiplexer_2 (.in0(out_4[0]), .in1(in_1[1]), .out(multiplexer_2_out), .sel(LOAD));
  Multiplexer multiplexer_3 (.in0(out_4[1]), .in1(in_1[2]), .out(multiplexer_3_out), .sel(LOAD));
  Multiplexer multiplexer_4 (.in0(out_4[2]), .in1(in_1[3]), .out(multiplexer_4_out), .sel(LOAD));
  D_Flip_Flop D0 (.D(multiplexer_1_out), .clk(in_3), .Q(out_4[0]));  // open: Qn, preset, reset
  D_Flip_Flop D1 (.D(multiplexer_2_out), .clk(in_3), .Q(out_4[1]));  // open: Qn, preset, reset
  D_Flip_Flop D2 (.D(multiplexer_3_out), .clk(in_3), .Q(out_4[2]));  // open: Qn, preset, reset
  D_Flip_Flop D3 (.D(multiplexer_4_out), .clk(in_3), .Q(out_4[3]));  // open: Qn, preset, reset
endmodule
