// Logisim project simple_cpu_2025_v2.circ as structural Verilog: 6 circuits, main circuit main
module main (
  input  [15:0] Instruction
);

  wire clock_1_out;
  wire [7:0] alu_1_r, multiplexer_1_out, registerbank_1_doutx, registerbank_1_douty, registerbank_1_r0_out,
       registerbank_1_r1_out, registerbank_1_r2_out, registerbank_1_r3_out;

  Clock clock_1 (.out(clock_1_out));
  Multiplexer #(.width(8)) multiplexer_1 (
    .in0(alu_1_r), .in1(Instruction[7:0]), .out(multiplexer_1_out), .sel(Instruction[15]));
  RegisterBank registerbank_1 (
    .Din(multiplexer_1_out), .Clock(clock_1_out), .Sel_X(Instruction[11:10]), .Sel_Write(Instruction[13:12]),
    .Write_Enable(Instruction[14]), .Sel_Y(Instruction[9:8]), .DoutX(registerbank_1_doutx),
    .DoutY(registerbank_1_douty), .R0_out(registerbank_1_r0_out), .R1_out(registerbank_1_r1_out),
    .R2_out(registerbank_1_r2_out), .R3_out(registerbank_1_r3_out));
  // Probe on registerbank_1_r0_out
  // Probe on registerbank_1_r1_out
  // Probe on registerbank_1_r2_out
  // Probe on registerbank_1_r3_out
  ALU alu_1 (.X(registerbank_1_doutx), .Y(registerbank_1_douty), .OP(Instruction[7]), .R(alu_1_r));
  // Probe on alu_1_r

  // Other names for the same wires on the sheet: Const[7:0] = Instruction[7:0]; Op_Type = Instruction[7];
  //   Write_En = Instruction[14]; ALU_Const = Instruction[15]; Sel_Write[1:0] = Instruction[13:12];
  //   Sel_X[1:0] = Instruction[11:10]; Sel_Y[1:0] = Instruction[9:8]

  // Notes on the sheet:
  //   OP_TYPE = 0, Somma
  //   OP_TYPE = 1, Sottrazione
  //   20 + 10 - 4
  //   R0 = 20
  //   R1 = 10
  //   R0 + R1 -> R2
  //   R3 = 4
  //   R2 - R3 -> R1
  //   R0 + R0 -> R0
endmodule

module FullAdder (
  input  Xn,
  input  Yn,
  input  Cn,
  output Sn,
  output Cn1
);

  wire and_1_out, and_2_out, and_3_out, and_4_out, and_5_out, and_6_out, and_7_out, and_8_out;

  and and_1 (and_1_out, ~Xn, ~Yn, Cn);  // AND_Gate
  and and_2 (and_2_out, ~Xn, Yn, ~Cn);  // AND_Gate
  and and_3 (and_3_out, Xn, ~Yn, ~Cn);  // AND_Gate
  and and_4 (and_4_out, Xn, Yn, Cn);
  and and_5 (and_5_out, ~Xn, Yn, Cn);  // AND_Gate
  and and_6 (and_6_out, Xn, ~Yn, Cn);  // AND_Gate
  and and_7 (and_7_out, Xn, Yn, ~Cn);  // AND_Gate
  and and_8 (and_8_out, Xn, Yn, Cn);
  or or_1 (Sn, and_1_out, and_2_out, and_3_out, and_4_out);
  or or_2 (Cn1, and_5_out, and_6_out, and_7_out, and_8_out);
endmodule

module HalfAdder (
  input  X0,
  input  Y0,
  output S0,
  output C1
);

  xor xor_1 (S0, X0, Y0);
  and and_1 (C1, X0, Y0);
endmodule

module controlled_not (
  input  [7:0] DataIn,
  input  C,
  output [7:0] DataOut
);

  xor xor_1 (DataOut[0], DataIn[0], C);
  xor xor_2 (DataOut[1], DataIn[1], C);
  xor xor_3 (DataOut[2], DataIn[2], C);
  xor xor_4 (DataOut[3], C, DataIn[3]);
  xor xor_5 (DataOut[4], DataIn[4], C);
  xor xor_6 (DataOut[5], DataIn[5], C);
  xor xor_7 (DataOut[6], DataIn[6], C);
  xor xor_8 (DataOut[7], C, DataIn[7]);
endmodule

module ALU (
  input  [7:0] X,
  input  [7:0] Y,
  input  OP,
  output [7:0] R
);

  wire fulladder_1_cn1, fulladder_2_cn1, fulladder_3_cn1, fulladder_4_cn1, fulladder_5_cn1, fulladder_6_cn1,
       fulladder_8_cn1;
  wire [7:0] controlled_not_1_dataout;

  controlled_not controlled_not_1 (.DataIn(Y), .C(OP), .DataOut(controlled_not_1_dataout));
  FullAdder fulladder_1 (
    .Xn(X[1]), .Yn(controlled_not_1_dataout[1]), .Cn(fulladder_8_cn1), .Sn(R[1]), .Cn1(fulladder_1_cn1));
  FullAdder fulladder_2 (
    .Xn(X[2]), .Yn(controlled_not_1_dataout[2]), .Cn(fulladder_1_cn1), .Sn(R[2]), .Cn1(fulladder_2_cn1));
  FullAdder fulladder_3 (
    .Xn(X[3]), .Yn(controlled_not_1_dataout[3]), .Cn(fulladder_2_cn1), .Sn(R[3]), .Cn1(fulladder_3_cn1));
  FullAdder fulladder_4 (
    .Xn(X[4]), .Yn(controlled_not_1_dataout[4]), .Cn(fulladder_3_cn1), .Sn(R[4]), .Cn1(fulladder_4_cn1));
  FullAdder fulladder_5 (
    .Xn(X[5]), .Yn(controlled_not_1_dataout[5]), .Cn(fulladder_4_cn1), .Sn(R[5]), .Cn1(fulladder_5_cn1));
  FullAdder fulladder_6 (
    .Xn(X[6]), .Yn(controlled_not_1_dataout[6]), .Cn(fulladder_5_cn1), .Sn(R[6]), .Cn1(fulladder_6_cn1));
  FullAdder fulladder_7 (.Xn(X[7]), .Yn(controlled_not_1_dataout[7]), .Cn(fulladder_6_cn1), .Sn(R[7]));  // open: Cn1
  FullAdder fulladder_8 (.Xn(X[0]), .Yn(controlled_not_1_dataout[0]), .Cn(OP), .Sn(R[0]), .Cn1(fulladder_8_cn1));

  // Notes on the sheet:
  //   OP = 0, R = X + Y
  //   OP = 1, R = X - Y
endmodule

module RegisterBank (
  input  [7:0] Din,
  input  Clock,
  input  [1:0] Sel_X,
  input  [1:0] Sel_Write,
  input  Write_Enable,
  input  [1:0] Sel_Y,
  output [7:0] DoutX,
  output [7:0] DoutY,
  output [7:0] R0_out,
  output [7:0] R1_out,
  output [7:0] R2_out,
  output [7:0] R3_out
);

  wire decoder_1_out0, decoder_1_out1, decoder_1_out2, decoder_1_out3;

  Decoder #(.select(2)) decoder_1 (
    .out0(decoder_1_out0), .out1(decoder_1_out1), .out2(decoder_1_out2), .out3(decoder_1_out3),
    .sel(Sel_Write), .en(Write_Enable));
  Register #(.trigger("falling")) R0 (.D(Din), .en(decoder_1_out0), .clk(Clock), .Q(R0_out));  // open: clr
  Register #(.trigger("falling")) R1 (.D(Din), .en(decoder_1_out1), .clk(Clock), .Q(R1_out));  // open: clr
  Register #(.trigger("falling")) R2 (.D(Din), .en(decoder_1_out2), .clk(Clock), .Q(R2_out));  // open: clr
  Register #(.trigger("falling")) R3 (.D(Din), .en(decoder_1_out3), .clk(Clock), .Q(R3_out));  // open: clr
  Multiplexer #(.select(2), .width(8)) multiplexer_1 (
    .in0(R0_out), .in1(R1_out), .in2(R2_out), .in3(R3_out), .out(DoutX), .sel(Sel_X));
  Multiplexer #(.select(2), .width(8)) multiplexer_2 (
    .in0(R0_out), .in1(R1_out), .in2(R2_out), .in3(R3_out), .out(DoutY), .sel(Sel_Y));
endmodule
