// Logisim project zero_to_max_binary_counter.circ as structural Verilog: 1 circuit, main circuit main
module main (
  input  [3:0] max,
  output [3:0] counter
);

  wire and_1_out, clock_1_out, xnor_1_out, xnor_2_out, xnor_3_out, xnor_4_out;

  Clock clock_1 (.out(clock_1_out));
  T_Flip_Flop t_ff_1 (.T(1'b1), .clk(clock_1_out), .Q(counter[0]), .reset(and_1_out));  // open: Qn, preset
  T_Flip_Flop #(.trigger("falling")) t_ff_2 (
    .T(1'b1), .clk(counter[0]), .Q(counter[1]), .reset(and_1_out));  // open: Qn, preset
  T_Flip_Flop #(.trigger("falling")) t_ff_3 (
    .T(1'b1), .clk(counter[1]), .Q(counter[2]), .reset(and_1_out));  // open: Qn, preset
  T_Flip_Flop #(.trigger("falling")) t_ff_4 (
    .T(1'b1), .clk(counter[2]), .Q(counter[3]), .reset(and_1_out));  // open: Qn, preset
  xnor xnor_1 (xnor_1_out, counter[0], max[0]);
  xnor xnor_2 (xnor_2_out, counter[1], max[1]);
  xnor xnor_3 (xnor_3_out, counter[2], max[2]);
  xnor xnor_4 (xnor_4_out, counter[3], max[3]);
  and and_1 (and_1_out, xnor_1_out, xnor_2_out, xnor_3_out, xnor_4_out);
endmodule
