// Logisim project 8_bit_adder.circ as structural Verilog: 3 circuits, main circuit main
module main (
  input  [7:0] X,
  input  [7:0] Y,
  output [7:0] SOMMA
);

  wire full_adder_1_cn1, full_adder_2_cn1, full_adder_3_cn1, full_adder_4_cn1, full_adder_5_cn1,
       full_adder_6_cn1, full_adder_7_cn1, half_adder_1_c1;

  HALF_ADDER half_adder_1 (.X0(X[0]), .Y0(Y[0]), .S0(SOMMA[0]), .C1(half_adder_1_c1));
  FULL_ADDER full_adder_1 (.Cn(half_adder_1_c1), .Xn(X[1]), .Yn(Y[1]), .Sn(SOMMA[1]), .Cn1(full_adder_1_cn1));
  FULL_ADDER full_adder_2 (.Cn(full_adder_1_cn1), .Xn(X[2]), .Yn(Y[2]), .Sn(SOMMA[2]), .Cn1(full_adder_2_cn1));
  FULL_ADDER full_adder_3 (.Cn(full_adder_2_cn1), .Xn(X[3]), .Yn(Y[3]), .Sn(SOMMA[3]), .Cn1(full_adder_3_cn1));
  FULL_ADDER full_adder_4 (.Cn(full_adder_3_cn1), .Xn(X[4]), .Yn(Y[4]), .Sn(SOMMA[4]), .Cn1(full_adder_4_cn1));
  FULL_ADDER full_adder_5 (.Cn(full_adder_4_cn1), .Xn(X[5]), .Yn(Y[5]), .Sn(SOMMA[5]), .Cn1(full_adder_5_cn1));
  FULL_ADDER full_adder_6 (.Cn(full_adder_5_cn1), .Xn(X[6]), .Yn(Y[6]), .Sn(SOMMA[6]), .Cn1(full_adder_6_cn1));
  FULL_ADDER full_adder_7 (.Cn(full_adder_6_cn1), .Xn(X[7]), .Yn(Y[7]), .Sn(SOMMA[7]), .Cn1(full_adder_7_cn1));
endmodule

module HALF_ADDER (
  input  X0,
  input  Y0,
  output S0,
  output C1
);

  wire and_1_out, and_2_out;

  and and_1 (and_1_out, ~X0, Y0);  // AND_Gate
  and and_2 (and_2_out, X0, ~Y0);  // AND_Gate
  and and_3 (C1, Y0, X0);
  or or_1 (S0, and_1_out, and_2_out);
endmodule

module FULL_ADDER (
  input  Cn,
  input  Xn,
  input  Yn,
  output Sn,
  output Cn1
);

  wire and_1_out, and_2_out, and_3_out, and_4_out, and_5_out, and_6_out, and_7_out;

  and and_1 (and_1_out, ~Cn, ~Xn, Yn);  // AND_Gate
  and and_2 (and_2_out, ~Cn, Xn, ~Yn);  // AND_Gate
  and and_3 (and_3_out, Cn, ~Xn, ~Yn);  // AND_Gate
  and and_4 (and_4_out, Cn, Xn, Yn);
  and and_5 (and_5_out, Cn, Xn);
  and and_6 (and_6_out, Cn, Yn);
  and and_7 (and_7_out, Xn, Yn);
  or or_1 (Sn, and_1_out, and_2_out, and_3_out, and_4_out);
  or or_2 (Cn1, and_5_out, and_6_out, and_7_out);
endmodule
