// Logisim project 8_bit_subtractor.circ as structural Verilog: 3 circuits, main circuit main
module main (
  input  [7:0] X,
  input  [7:0] Y,
  output [7:0] SOMMA
);

  wire full_adder_1_cn1, full_adder_2_cn1, full_adder_3_cn1, full_adder_4_cn1, full_adder_5_cn1,
       full_adder_6_cn1, full_adder_7_cn1, full_adder_8_cn1, not_1_out, not_2_out, not_3_out, not_4_out,
       not_5_out, not_6_out, not_7_out, not_8_out;

  not not_1 (not_1_out, Y[7]);
  not not_2 (not_2_out, Y[0]);
  not not_3 (not_3_out, Y[1]);
  not not_4 (not_4_out, Y[2]);
  not not_5 (not_5_out, Y[3]);
  not not_6 (not_6_out, Y[4]);
  not not_7 (not_7_out, Y[5]);
  not not_8 (not_8_out, Y[6]);
  FULL_ADDER full_adder_1 (.Cn(1'b1), .Xn(X[0]), .Yn(not_2_out), .Sn(SOMMA[0]), .Cn1(full_adder_1_cn1));
  FULL_ADDER full_adder_2 (.Cn(full_adder_1_cn1), .Xn(X[1]), .Yn(not_3_out), .Sn(SOMMA[1]), .Cn1(full_adder_2_cn1));
  FULL_ADDER full_adder_3 (.Cn(full_adder_2_cn1), .Xn(X[2]), .Yn(not_4_out), .Sn(SOMMA[2]), .Cn1(full_adder_3_cn1));
  FULL_ADDER full_adder_4 (.Cn(full_adder_3_cn1), .Xn(X[3]), .Yn(not_5_out), .Sn(SOMMA[3]), .Cn1(full_adder_4_cn1));
  FULL_ADDER full_adder_5 (.Cn(full_adder_4_cn1), .Xn(X[4]), .Yn(not_6_out), .Sn(SOMMA[4]), .Cn1(full_adder_5_cn1));
  FULL_ADDER full_adder_6 (.Cn(full_adder_5_cn1), .Xn(X[5]), .Yn(not_7_out), .Sn(SOMMA[5]), .Cn1(full_adder_6_cn1));
  FULL_ADDER full_adder_7 (.Cn(full_adder_6_cn1), .Xn(X[6]), .Yn(not_8_out), .Sn(SOMMA[6]), .Cn1(full_adder_7_cn1));
  FULL_ADDER full_adder_8 (.Cn(full_adder_7_cn1), .Xn(X[7]), .Yn(not_1_out), .Sn(SOMMA[7]), .Cn1(full_adder_8_cn1));
endmodule

module HALF_ADDER (
  input  X0,
  input  Y0,
  output S0,
  output C1
);

  wire and_1_out, and_2_out;

  and and_1 (and_1_out, ~X0, Y0);  // AND_Gate
  and and_2 (and_2_out, X0, ~Y0);  // AND_Gate
  and and_3 (C1, Y0, X0);
  or or_1 (S0, and_1_out, and_2_out);
endmodule

module FULL_ADDER (
  input  Cn,
  input  Xn,
  input  Yn,
  output Sn,
  output Cn1
);

  wire and_1_out, and_2_out, and_3_out, and_4_out, and_5_out, and_6_out, and_7_out;

  and and_1 (and_1_out, ~Cn, ~Xn, Yn);  // AND_Gate
  and and_2 (and_2_out, ~Cn, Xn, ~Yn);  // AND_Gate
  and and_3 (and_3_out, Cn, ~Xn, ~Yn);  // AND_Gate
  and and_4 (and_4_out, Cn, Xn, Yn);
  and and_5 (and_5_out, Cn, Xn);
  and and_6 (and_6_out, Cn, Yn);
  and and_7 (and_7_out, Xn, Yn);
  or or_1 (Sn, and_1_out, and_2_out, and_3_out, and_4_out);
  or or_2 (Cn1, and_5_out, and_6_out, and_7_out);
endmodule
