// Logisim project 3bit_counter.circ as structural Verilog: 1 circuit, main circuit main
module main (
  output b2,
  output b1,
  output b0
);

  wire clock_1_out;

  Clock clock_1 (.out(clock_1_out));
  T_Flip_Flop #(.trigger("falling")) t_ff_1 (.T(1'b1), .clk(clock_1_out), .Q(b0));  // open: Qn, reset, preset
  T_Flip_Flop #(.trigger("falling")) t_ff_2 (.T(1'b1), .clk(b0), .Q(b1));  // open: Qn, reset, preset
  T_Flip_Flop #(.trigger("falling")) t_ff_3 (.T(1'b1), .clk(b1), .Q(b2));  // open: Qn, reset, preset
endmodule
