// Logisim project 8bit_adder.circ as structural Verilog: 3 circuits, main circuit main
module main (
  input  x7,
  input  x6,
  input  x5,
  input  x4,
  input  x3,
  input  x2,
  input  x1,
  input  x0,
  input  in_9,
  input  y6,
  input  y5,
  input  y4,
  input  y3,
  input  y2,
  input  y1,
  input  y0
);

  wire fulladder_1_c, fulladder_2_c, fulladder_3_c, fulladder_4_c, fulladder_5_c, fulladder_6_c,
       fulladder_7_c, halfadder_1_c;
  wire [7:0] halfadder_1_s;

  // Probe on {x7, x6, x5, x4, x3, x2, x1, x0}
  // Probe on {in_9, y6, y5, y4, y3, y2, y1, y0}
  // Probe on fulladder_7_c
  // Probe on halfadder_1_s
  HalfAdder halfadder_1 (.a(x0), .b(y0), .s(halfadder_1_s[0]), .c(halfadder_1_c));
  FullAdder fulladder_1 (.carry_in(halfadder_1_c), .a(x1), .b(y1), .s(halfadder_1_s[1]), .c(fulladder_1_c));
  FullAdder fulladder_2 (.carry_in(fulladder_1_c), .a(x2), .b(y2), .s(halfadder_1_s[2]), .c(fulladder_2_c));
  FullAdder fulladder_3 (.carry_in(fulladder_2_c), .a(x3), .b(y3), .s(halfadder_1_s[3]), .c(fulladder_3_c));
  FullAdder fulladder_4 (.carry_in(fulladder_3_c), .a(x4), .b(y4), .s(halfadder_1_s[4]), .c(fulladder_4_c));
  FullAdder fulladder_5 (.carry_in(fulladder_4_c), .a(x5), .b(y5), .s(halfadder_1_s[5]), .c(fulladder_5_c));
  FullAdder fulladder_6 (.carry_in(fulladder_5_c), .a(x6), .b(y6), .s(halfadder_1_s[6]), .c(fulladder_6_c));
  FullAdder fulladder_7 (.carry_in(fulladder_6_c), .a(x7), .b(in_9), .s(halfadder_1_s[7]), .c(fulladder_7_c));
  // Probe on halfadder_1_s[7]
  // Probe on halfadder_1_s[6]
  // Probe on halfadder_1_s[4]
  // Probe on halfadder_1_s[5]
  // Probe on halfadder_1_s[3]
  // Probe on halfadder_1_s[2]
  // Probe on halfadder_1_s[0]
  // Probe on halfadder_1_s[1]
endmodule

module HalfAdder (
  input  a,
  input  b,
  output s,
  output c
);

  xor xor_1 (s, a, b);
  and and_1 (c, b, a);
endmodule

module FullAdder (
  input  carry_in,
  input  a,
  input  b,
  output s,
  output c
);

  wire and_1_out, and_2_out, and_3_out, and_4_out, and_5_out, and_6_out, and_7_out;

  and and_1 (and_1_out, ~carry_in, ~a, b);  // AND_Gate
  and and_2 (and_2_out, ~carry_in, a, ~b);  // AND_Gate
  and and_3 (and_3_out, carry_in, ~a, ~b);  // AND_Gate
  and and_4 (and_4_out, carry_in, a, b);
  and and_5 (and_5_out, a, b);
  and and_6 (and_6_out, carry_in, b);
  and and_7 (and_7_out, carry_in, a);
  or or_1 (s, and_1_out, and_2_out, and_3_out, and_4_out);
  or or_2 (c, and_5_out, and_6_out, and_7_out);
endmodule
