// Logisim project 8bit_register.circ as structural Verilog: 1 circuit, main circuit main
module main (
  input  [7:0] D,
  input  CLOCK,
  output [7:0] out_3
);

  D_Flip_Flop #(.trigger("high")) d_ff_1 (.D(D[0]), .clk(CLOCK), .Q(out_3[0]));  // open: Qn, preset, reset
  D_Flip_Flop #(.trigger("high")) d_ff_2 (.D(D[1]), .clk(CLOCK), .Q(out_3[1]));  // open: Qn, preset, reset
  D_Flip_Flop #(.trigger("high")) d_ff_3 (.D(D[2]), .clk(CLOCK), .Q(out_3[2]));  // open: Qn, preset, reset
  D_Flip_Flop #(.trigger("high")) d_ff_4 (.D(D[3]), .clk(CLOCK), .Q(out_3[3]));  // open: Qn, preset, reset
  D_Flip_Flop #(.trigger("high")) d_ff_5 (.D(D[4]), .clk(CLOCK), .Q(out_3[4]));  // open: Qn, preset, reset
  D_Flip_Flop #(.trigger("high")) d_ff_6 (.D(D[5]), .clk(CLOCK), .Q(out_3[5]));  // open: Qn, preset, reset
  D_Flip_Flop #(.trigger("high")) d_ff_7 (.D(D[6]), .clk(CLOCK), .Q(out_3[6]));  // open: Qn, preset, reset
  D_Flip_Flop #(.trigger("high")) d_ff_8 (.D(D[7]), .clk(CLOCK), .Q(out_3[7]));  // open: Qn, preset, reset
endmodule
