// Logisim project change_sign.circ as structural Verilog: 1 circuit, main circuit main
module main (
  input  [7:0] in_1,
  output [7:0] out_2,
  output [7:0] out_3
);

  wire [7:0] not_5_out;

  not not_1 (not_5_out[1], in_1[1]);
  not not_2 (not_5_out[3], in_1[3]);
  not not_3 (not_5_out[5], in_1[5]);
  not not_4 (not_5_out[7], in_1[7]);
  not not_5 (not_5_out[0], in_1[0]);
  not not_6 (not_5_out[2], in_1[2]);
  not not_7 (not_5_out[4], in_1[4]);
  not not_8 (not_5_out[6], in_1[6]);
  Adder adder_1 (.a(not_5_out), .b(8'h1), .out(out_2));  // open: cin, cout

  assign out_3 = out_2;
endmodule
