// Logisim project counter_with_limit.circ as structural Verilog: 2 circuits, main circuit main
module main (
  input  CLR,
  output [5:0] out_2
);

  wire and_1_out, clock_1_out, or_1_out;

  Clock clock_1 (.out(clock_1_out));
  or or_1 (or_1_out, CLR, and_1_out);
  and and_1 (and_1_out, ~out_2[5], out_2[4], out_2[3], out_2[2], out_2[1], ~out_2[0]);  // AND_Gate
  contatore contatore_1 (
    .CLK(clock_1_out), .CLR(or_1_out), .b5(out_2[5]), .b4(out_2[4]), .b3(out_2[3]), .b2(out_2[2]),
    .b1(out_2[1]), .b0(out_2[0]));
endmodule

module contatore (
  input  CLK,
  input  CLR,
  output b5,
  output b4,
  output b3,
  output b2,
  output b1,
  output b0
);

  T_Flip_Flop #(.trigger("falling")) t_ff_1 (.T(1'b1), .clk(CLK), .Q(b0), .reset(CLR));  // open: Qn, preset
  T_Flip_Flop #(.trigger("falling")) t_ff_2 (.T(1'b1), .clk(b0), .Q(b1), .reset(CLR));  // open: Qn, preset
  T_Flip_Flop #(.trigger("falling")) t_ff_3 (.T(1'b1), .clk(b1), .Q(b2), .reset(CLR));  // open: Qn, preset
  T_Flip_Flop #(.trigger("falling")) t_ff_4 (.T(1'b1), .clk(b2), .Q(b3), .reset(CLR));  // open: Qn, preset
  T_Flip_Flop #(.trigger("falling")) t_ff_5 (.T(1'b1), .clk(b3), .Q(b4), .reset(CLR));  // open: Qn, preset
  T_Flip_Flop #(.trigger("falling")) t_ff_6 (.T(1'b1), .clk(b4), .Q(b5), .reset(CLR));  // open: Qn, preset
endmodule
