// Logisim project flip_flop_set_reset_gated.circ as structural Verilog: 1 circuit, main circuit main
module main (
  input  S,
  input  Write,
  input  R,
  output Q,
  output nQ
);

  wire nand_1_out, nand_2_out;

  nand nand_1 (nand_1_out, S, Write);
  nand nand_2 (nand_2_out, Write, R);
  nand nand_3 (Q, nand_1_out, nQ);
  nand nand_4 (nQ, Q, nand_2_out);

  // Notes on the sheet:
  //   S: initial=0x1
  //   Write: initial=0x1
endmodule
