// Logisim project io_system.circ as structural Verilog: 1 circuit, main circuit main
module main (
  input  [7:0] ADDR_BUS,
  input  MEM_R,
  input  in_3,
  input  in_4,
  input  in_5,
  input  in_6,
  input  in_7,
  input  in_8,
  input  in_9,
  input  in_10,
  output [7:0] DATA_BUS
);

  wire and_1_out, and_2_out, clock_1_out, not_1_out;
  wire [7:0] controlled_buffer_1_out, counter_1_q, ram_1_dout;

  Counter counter_1 (.clk(clock_1_out), .Q(counter_1_q));  // open: clr, load, up, count, D, carry
  Clock clock_1 (.out(clock_1_out));
  RAM #(.addrWidth(7), .enables("line")) ram_1 (
    .addr(ADDR_BUS[6:0]), .din(DATA_BUS), .dout(ram_1_dout));  // open: we, clk
  and and_1 (and_1_out, ~ADDR_BUS[0], ~ADDR_BUS[1], ~ADDR_BUS[2], ~ADDR_BUS[3], ~ADDR_BUS[4], ~ADDR_BUS[5], ~ADDR_BUS[6], ADDR_BUS[7]);  // AND_Gate
  and and_2 (and_2_out, ADDR_BUS[0], ~ADDR_BUS[1], ~ADDR_BUS[2], ~ADDR_BUS[3], ~ADDR_BUS[4], ~ADDR_BUS[5], ~ADDR_BUS[6], ADDR_BUS[7]);  // AND_Gate
  not not_1 (not_1_out, ADDR_BUS[7]);
  assign controlled_buffer_1_out = not_1_out ? ram_1_dout : 8'bz;  // Controlled_Buffer controlled_buffer_1
  assign DATA_BUS = MEM_R ? controlled_buffer_1_out : 8'bz;  // Controlled_Buffer controlled_buffer_2
  assign controlled_buffer_1_out = and_1_out ? {in_10, in_9, in_8, in_7, in_6, in_5, in_4, in_3} : 8'bz;  // Controlled_Buffer controlled_buffer_3
  assign controlled_buffer_1_out = and_2_out ? counter_1_q : 8'bz;  // Controlled_Buffer controlled_buffer_4

  // Notes on the sheet:
  //   Keyboard, addr = 0x80
  //   addr = 1000 0000
  //   RTC, addr = 0x81
  //   0000 0000 : 0111 1111
endmodule
