// Logisim project logic_circuits_with_mos.circ as structural Verilog: 1 circuit, main circuit main
module main (
  input  in_1,
  input  in_2,
  input  in_3,
  input  in_4,
  input  in_5,
  output out_6,
  output out_7,
  output out_8,
  output out_9,
  output out_10,
  output out_11
);

  wire transistor_6_out, transistor_7_out;

  Transistor transistor_1 (.in(1'b1), .out(out_7), .gate(in_3));
  Transistor #(.\type ("n")) transistor_2 (.in(1'b0), .out(out_7), .gate(in_3));
  not not_1 (out_9, in_3);
  Transistor transistor_3 (.in(1'b1), .out(out_8), .gate(in_2));
  nand nand_1 (out_11, in_2, in_5);
  Transistor transistor_4 (.in(1'b1), .out(out_8), .gate(in_5));
  Transistor #(.\type ("n")) transistor_5 (.in(transistor_6_out), .out(out_8), .gate(in_5));
  Transistor #(.\type ("n")) transistor_6 (.in(1'b0), .out(transistor_6_out), .gate(in_2));
  Transistor transistor_7 (.in(1'b1), .out(transistor_7_out), .gate(in_1));
  Transistor transistor_8 (.in(transistor_7_out), .out(out_6), .gate(in_4));
  Transistor #(.\type ("n")) transistor_9 (.in(1'b0), .out(out_6), .gate(in_1));
  Transistor #(.\type ("n")) transistor_10 (.in(1'b0), .out(out_6), .gate(in_4));
  nor nor_1 (out_10, in_1, in_4);
endmodule
