// Logisim project ode_to_joy.circ as structural Verilog: 2 circuits, main circuit main
module main (
  input  in_1
);

  wire clock_1_out;
  wire [4:0] counter_1_q;
  wire [7:0] rom_1_data;

  Clock clock_1 (.out(clock_1_out));
  Counter #(.max('h1f), .width(5)) counter_1 (
    .clr(in_1), .clk(clock_1_out), .Q(counter_1_q));  // open: load, up, count, D, carry
  ROM #(.addrWidth(5)) rom_1 (.addr(counter_1_q), .data(rom_1_data));
  Tone tone_1 (
    .Do(rom_1_data[0]), .Re(rom_1_data[1]), .Mi(rom_1_data[2]), .Fa(rom_1_data[3]), .Sol(rom_1_data[4]),
    .La(rom_1_data[5]), .Si(rom_1_data[6]), .Do8(rom_1_data[7]));

  // Notes on the sheet:
  //   contents of rom_1 (hex, n*v repeats v):
  //   4 4 8 10 10 8 4 2 1 1 2 4 4 4 2 2 4 4 8 10 10 8 4 2 1 1 2 4 2 2 1 1
endmodule

module Tone (
  input  Do,
  input  Re,
  input  Mi,
  input  Fa,
  input  Sol,
  input  La,
  input  Si,
  input  Do8
);

  // Buzzer buzzer_1: pin names not known; wires that end beside it: 14'h20b, Do, {7{1'b1}}
  // Buzzer buzzer_2: pin names not known; wires that end beside it: 14'h24b, Re, {7{1'b1}}
  // Buzzer buzzer_3: pin names not known; wires that end beside it: 14'h293, Mi, {7{1'b1}}
  // Buzzer buzzer_4: pin names not known; wires that end beside it: 14'h2bb, Fa, {7{1'b1}}
  // Buzzer buzzer_5: pin names not known; wires that end beside it: 14'h310, Sol, {7{1'b1}}
  // Buzzer buzzer_6: pin names not known; wires that end beside it: 14'h370, La, {7{1'b1}}
  // Buzzer buzzer_7: pin names not known; wires that end beside it: 14'h3dc, Si, {7{1'b1}}
  // Buzzer buzzer_8: pin names not known; wires that end beside it: 14'h416, Do8, {7{1'b1}}
endmodule
