// Logisim project priority_encoder.circ as structural Verilog: 1 circuit, main circuit main
module main (
  input  x0,
  input  x1,
  input  x2,
  input  x3,
  input  x4,
  input  x5,
  input  x6,
  input  x7,
  output y2,
  output y1,
  output y0
);

  wire and_1_out, and_2_out, and_3_out, and_4_out, and_5_out, and_6_out, and_7_out, and_9_out, and_10_out,
       and_11_out, or_1_out, or_2_out, or_3_out;

  and and_1 (and_1_out, ~x4, x5);  // AND_Gate
  and and_2 (and_2_out, ~x4, ~x5, x6);  // AND_Gate
  and and_3 (and_3_out, ~x4, ~x5, ~x6, x7);  // AND_Gate
  and and_4 (and_4_out, ~x2, x3);  // AND_Gate
  and and_5 (and_5_out, ~x2, ~x3, ~x4, ~x5, x6);  // AND_Gate
  and and_6 (and_6_out, ~x2, ~x3, ~x4, ~x5, ~x6, x7);  // AND_Gate
  and and_7 (and_7_out, ~x5, ~x6, x7);  // AND_Gate
  or or_1 (or_1_out, x2, and_4_out, and_5_out, and_6_out);
  or or_2 (or_2_out, x5, and_7_out);
  or or_3 (or_3_out, x4, and_1_out, and_2_out, and_3_out);
  and and_8 (y1, ~x0, ~x1, or_1_out);  // AND_Gate
  and and_9 (and_9_out, or_2_out, ~x0, ~x1, ~x2, ~x3, ~x4);  // AND_Gate
  and and_10 (and_10_out, ~x0, x1);  // AND_Gate
  and and_11 (and_11_out, ~x0, ~x1, ~x2, x3);  // AND_Gate
  and and_12 (y2, ~x0, ~x1, ~x2, ~x3, or_3_out);  // AND_Gate
  or or_4 (y0, and_9_out, and_10_out, and_11_out);
endmodule
