// Logisim project priority_encoder_with_block_circuit.circ as structural Verilog: 1 circuit, main circuit main
module main (
  input  x0,
  input  x1,
  input  x2,
  input  x3,
  input  x4,
  input  x5,
  input  x6,
  input  x7,
  output y2,
  output y1,
  output y0
);

  Priority_Encoder priority_encoder_1 (
    .in0(x0), .in1(x1), .in2(x2), .in3(x3), .in4(x4), .in5(x5), .in6(x6), .in7(x7), .out({y2, y1, y0}));  // open: en_in, gs, en_out
endmodule
