// Logisim project register_bank.circ as structural Verilog: 1 circuit, main circuit main
module main (
  input  [1:0] ADDRESS,
  input  [7:0] DataIn,
  input  WE,
  input  CLR,
  output [7:0] DataOut
);

  wire clock_1_out, decoder_1_out0, decoder_1_out1, decoder_1_out2, decoder_1_out3;
  wire [7:0] R0_q, R1_q, R2_q, R3_q;

  Clock clock_1 (.out(clock_1_out));
  Decoder #(.select(2)) decoder_1 (
    .out0(decoder_1_out0), .out1(decoder_1_out1), .out2(decoder_1_out2), .out3(decoder_1_out3),
    .sel(ADDRESS), .en(WE));
  Register R0 (.D(DataIn), .en(decoder_1_out0), .clk(clock_1_out), .Q(R0_q), .clr(CLR));
  Register R1 (.D(DataIn), .en(decoder_1_out1), .clk(clock_1_out), .Q(R1_q), .clr(CLR));
  Register R2 (.D(DataIn), .en(decoder_1_out2), .clk(clock_1_out), .Q(R2_q), .clr(CLR));
  Register R3 (.D(DataIn), .en(decoder_1_out3), .clk(clock_1_out), .Q(R3_q), .clr(CLR));
  Multiplexer #(.select(2), .width(8)) multiplexer_1 (
    .in0(R0_q), .in1(R1_q), .in2(R2_q), .in3(R3_q), .out(DataOut), .sel(ADDRESS));
endmodule
