// Logisim project simple_cpu.circ as structural Verilog: 2 circuits, main circuit main
module main (
  input  [7:0] Const,
  input  in_2,
  input  SelConst,
  input  [1:0] SelX,
  input  [1:0] SelY,
  input  [1:0] SelDest,
  output [7:0] out_7
);

  wire clock_1_out, decoder_1_out0, decoder_1_out1, decoder_1_out2, decoder_1_out3;
  wire [7:0] multiplexer_1_out, multiplexer_2_out, multiplexer_3_out, R0_q, R1_q, R2_q, R3_q;

  Decoder #(.select(2)) decoder_1 (
    .out0(decoder_1_out0), .out1(decoder_1_out1), .out2(decoder_1_out2), .out3(decoder_1_out3), .sel(SelDest));  // open: en
  Clock clock_1 (.out(clock_1_out));
  Multiplexer #(.width(8)) multiplexer_1 (.in0(out_7), .in1(Const), .out(multiplexer_1_out), .sel(SelConst));
  Register R0 (.D(multiplexer_1_out), .en(decoder_1_out0), .clk(clock_1_out), .Q(R0_q));  // open: clr
  Register R1 (.D(multiplexer_1_out), .en(decoder_1_out1), .clk(clock_1_out), .Q(R1_q));  // open: clr
  Register R2 (.D(multiplexer_1_out), .en(decoder_1_out2), .clk(clock_1_out), .Q(R2_q));  // open: clr
  Register R3 (.D(multiplexer_1_out), .en(decoder_1_out3), .clk(clock_1_out), .Q(R3_q));  // open: clr
  Multiplexer #(.select(2), .width(8)) multiplexer_2 (
    .in0(R0_q), .in1(R1_q), .in2(R2_q), .in3(R3_q), .out(multiplexer_2_out), .sel(SelX));
  Multiplexer #(.select(2), .width(8)) multiplexer_3 (
    .in0(R0_q), .in1(R1_q), .in2(R2_q), .in3(R3_q), .out(multiplexer_3_out), .sel(SelY));
  ALU alu_1 (.X(multiplexer_2_out), .Operation(in_2), .Y(multiplexer_3_out), .Res(out_7));
endmodule

module ALU (
  input  [7:0] X,
  input  Operation,
  input  [7:0] Y,
  output [7:0] Res
);

  wire [7:0] xor_1_out;

  xor xor_1 (xor_1_out[0], Y[0], Operation);
  xor xor_2 (xor_1_out[1], Y[1], Operation);
  xor xor_3 (xor_1_out[2], Y[2], Operation);
  xor xor_4 (xor_1_out[3], Y[3], Operation);
  xor xor_5 (xor_1_out[4], Y[4], Operation);
  xor xor_6 (xor_1_out[5], Y[5], Operation);
  xor xor_7 (xor_1_out[6], Y[6], Operation);
  xor xor_8 (xor_1_out[7], Y[7], Operation);
  Adder adder_1 (.a(X), .b(xor_1_out), .out(Res), .cin(Operation));  // open: cout
endmodule
