// Logisim project simple_cpu.circ as structural Verilog: 3 circuits, main circuit main
module main (
  input  RESET,
  output [7:0] out_2
);

  wire clock_1_out, decoder_1_out0, decoder_1_out1, decoder_1_out2, decoder_1_out3, Op, SelConst;
  wire [1:0] SelDest, SelX, SelY;
  wire [2:0] programcounter_1_b0;
  wire [7:0] Const, multiplexer_1_out, multiplexer_2_out, multiplexer_3_out, R0_q, R1_q, R2_q, R3_q;

  Decoder #(.select(2)) decoder_1 (
    .out0(decoder_1_out0), .out1(decoder_1_out1), .out2(decoder_1_out2), .out3(decoder_1_out3), .sel(SelDest));  // open: en
  Clock clock_1 (.out(clock_1_out));
  Multiplexer #(.width(8)) multiplexer_1 (.in0(out_2), .in1(Const), .out(multiplexer_1_out), .sel(SelConst));
  Register R0 (.D(multiplexer_1_out), .en(decoder_1_out0), .clk(clock_1_out), .Q(R0_q), .clr(RESET));
  Register R1 (.D(multiplexer_1_out), .en(decoder_1_out1), .clk(clock_1_out), .Q(R1_q), .clr(RESET));
  Register R2 (.D(multiplexer_1_out), .en(decoder_1_out2), .clk(clock_1_out), .Q(R2_q), .clr(RESET));
  ProgramCounter programcounter_1 (
    .CLK(clock_1_out), .CLEAR(RESET), .b2(programcounter_1_b0[2]), .b1(programcounter_1_b0[1]),
    .b0(programcounter_1_b0[0]));
  Register R3 (.D(multiplexer_1_out), .en(decoder_1_out3), .clk(clock_1_out), .Q(R3_q), .clr(RESET));
  ROM #(.addrWidth(3), .dataWidth(16)) rom_1 (
    .addr(programcounter_1_b0), .data({Op, SelY, SelX, SelDest, SelConst, Const}));
  Multiplexer #(.select(2), .width(8)) multiplexer_2 (
    .in0(R0_q), .in1(R1_q), .in2(R2_q), .in3(R3_q), .out(multiplexer_2_out), .sel(SelX));
  Multiplexer #(.select(2), .width(8)) multiplexer_3 (
    .in0(R0_q), .in1(R1_q), .in2(R2_q), .in3(R3_q), .out(multiplexer_3_out), .sel(SelY));
  ALU alu_1 (.X(multiplexer_2_out), .Operation(Op), .Y(multiplexer_3_out), .Res(out_2));

  // Notes on the sheet:
  //   contents of rom_1 (hex, n*v repeats v):
  //   31e 528 b600 105
endmodule

module ALU (
  input  [7:0] X,
  input  Operation,
  input  [7:0] Y,
  output [7:0] Res
);

  wire [7:0] xor_1_out;

  xor xor_1 (xor_1_out[0], Y[0], Operation);
  xor xor_2 (xor_1_out[1], Y[1], Operation);
  xor xor_3 (xor_1_out[2], Y[2], Operation);
  xor xor_4 (xor_1_out[3], Y[3], Operation);
  xor xor_5 (xor_1_out[4], Y[4], Operation);
  xor xor_6 (xor_1_out[5], Y[5], Operation);
  xor xor_7 (xor_1_out[6], Y[6], Operation);
  xor xor_8 (xor_1_out[7], Y[7], Operation);
  Adder adder_1 (.a(X), .b(xor_1_out), .out(Res), .cin(Operation));  // open: cout
endmodule

module ProgramCounter (
  input  CLK,
  input  CLEAR,
  output b2,
  output b1,
  output b0
);

  T_Flip_Flop #(.trigger("falling")) t_ff_1 (.T(1'b1), .clk(CLK), .Q(b0), .reset(CLEAR));  // open: Qn, preset
  T_Flip_Flop #(.trigger("falling")) t_ff_2 (.T(1'b1), .clk(b0), .Q(b1), .reset(CLEAR));  // open: Qn, preset
  T_Flip_Flop #(.trigger("falling")) t_ff_3 (.T(1'b1), .clk(b1), .Q(b2), .reset(CLEAR));  // open: Qn, preset
endmodule
