// Logisim project sottrattore.circ as structural Verilog: 3 circuits, main circuit main
module main (
  input  [3:0] X,
  input  [3:0] Y,
  output [3:0] S0
);

  wire fulladder_1_cn1, fulladder_2_cn1, fulladder_3_cn1, halfadder_1_c1;

  HalfAdder halfadder_1 (.X0(X[0]), .Y0(Y[0]), .S0(S0[0]), .C1(halfadder_1_c1));
  FullAdder fulladder_1 (.Xn(X[1]), .Yn(Y[1]), .Cn(halfadder_1_c1), .Sn(S0[1]), .Cn1(fulladder_1_cn1));
  FullAdder fulladder_2 (.Xn(X[2]), .Yn(Y[2]), .Cn(fulladder_1_cn1), .Sn(S0[2]), .Cn1(fulladder_2_cn1));
  FullAdder fulladder_3 (.Xn(X[3]), .Yn(Y[3]), .Cn(fulladder_2_cn1), .Sn(S0[3]), .Cn1(fulladder_3_cn1));
endmodule

module FullAdder (
  input  Xn,
  input  Yn,
  input  Cn,
  output Sn,
  output Cn1
);

  wire and_1_out, and_2_out, and_3_out, and_4_out, and_5_out, and_6_out, and_7_out, and_8_out;

  and and_1 (and_1_out, ~Xn, ~Yn, Cn);  // AND_Gate
  and and_2 (and_2_out, ~Xn, Yn, ~Cn);  // AND_Gate
  and and_3 (and_3_out, Xn, ~Yn, ~Cn);  // AND_Gate
  and and_4 (and_4_out, Xn, Yn, Cn);
  and and_5 (and_5_out, ~Xn, Yn, Cn);  // AND_Gate
  and and_6 (and_6_out, Xn, ~Yn, Cn);  // AND_Gate
  and and_7 (and_7_out, Xn, Yn, ~Cn);  // AND_Gate
  and and_8 (and_8_out, Xn, Yn, Cn);
  or or_1 (Sn, and_1_out, and_2_out, and_3_out, and_4_out);
  or or_2 (Cn1, and_5_out, and_6_out, and_7_out, and_8_out);
endmodule

module HalfAdder (
  input  X0,
  input  Y0,
  output S0,
  output C1
);

  xor xor_1 (S0, X0, Y0);
  and and_1 (C1, X0, Y0);
endmodule
