// Logisim project sum_subtract.circ as structural Verilog: 1 circuit, main circuit main
module main (
  input  [7:0] X,
  input  Operation,
  input  [7:0] Y,
  output [7:0] out_4
);

  wire [7:0] xor_1_out;

  xor xor_1 (xor_1_out[0], Y[0], Operation);
  xor xor_2 (xor_1_out[1], Y[1], Operation);
  xor xor_3 (xor_1_out[2], Y[2], Operation);
  xor xor_4 (xor_1_out[3], Y[3], Operation);
  xor xor_5 (xor_1_out[4], Y[4], Operation);
  xor xor_6 (xor_1_out[5], Y[5], Operation);
  xor xor_7 (xor_1_out[6], Y[6], Operation);
  xor xor_8 (xor_1_out[7], Y[7], Operation);
  Adder adder_1 (.a(X), .b(xor_1_out), .out(out_4), .cin(Operation));  // open: cout
endmodule
