// Logisim project zero_match.circ as structural Verilog: 1 circuit, main circuit main
module main (
  input  [7:0] in_1,
  output Zero
);

  nor nor_1 (Zero, in_1[0], in_1[1], in_1[2], in_1[3], in_1[4], in_1[5], in_1[6], in_1[7]);
endmodule
