// Logisim project zero_to_nine_binary_counter.circ as structural Verilog: 1 circuit, main circuit main
module main (
  output [3:0] out_1
);

  wire and_1_out, clock_1_out;

  Clock clock_1 (.out(clock_1_out));
  T_Flip_Flop t_ff_1 (.T(1'b1), .clk(clock_1_out), .Q(out_1[0]), .reset(and_1_out));  // open: Qn, preset
  T_Flip_Flop #(.trigger("falling")) t_ff_2 (
    .T(1'b1), .clk(out_1[0]), .Q(out_1[1]), .reset(and_1_out));  // open: Qn, preset
  T_Flip_Flop #(.trigger("falling")) t_ff_3 (
    .T(1'b1), .clk(out_1[1]), .Q(out_1[2]), .reset(and_1_out));  // open: Qn, preset
  T_Flip_Flop #(.trigger("falling")) t_ff_4 (
    .T(1'b1), .clk(out_1[2]), .Q(out_1[3]), .reset(and_1_out));  // open: Qn, preset
  and and_1 (and_1_out, ~out_1[0], out_1[1], ~out_1[2], out_1[3]);  // AND_Gate
endmodule
