// Logisim project counter_4_bit_with_limit.circ as structural Verilog: 1 circuit, main circuit main
module main (
  input  [3:0] Limit,
  output [3:0] out_2
);

  wire and_1_out, clock_1_out, xnor_1_out, xnor_2_out, xnor_3_out, xnor_4_out;

  Clock clock_1 (.out(clock_1_out));
  T_Flip_Flop t_ff_1 (.T(1'b1), .clk(clock_1_out), .Q(out_2[0]), .reset(and_1_out));  // open: Qn, preset
  T_Flip_Flop #(.trigger("falling")) t_ff_2 (
    .T(1'b1), .clk(out_2[0]), .Q(out_2[1]), .reset(and_1_out));  // open: Qn, preset
  T_Flip_Flop #(.trigger("falling")) t_ff_3 (
    .T(1'b1), .clk(out_2[1]), .Q(out_2[2]), .reset(and_1_out));  // open: Qn, preset
  T_Flip_Flop #(.trigger("falling")) t_ff_4 (
    .T(1'b1), .clk(out_2[2]), .Q(out_2[3]), .reset(and_1_out));  // open: Qn, preset
  xnor xnor_1 (xnor_1_out, out_2[0], Limit[0]);
  xnor xnor_2 (xnor_2_out, out_2[1], Limit[1]);
  xnor xnor_3 (xnor_3_out, out_2[2], Limit[2]);
  xnor xnor_4 (xnor_4_out, out_2[3], Limit[3]);
  and and_1 (and_1_out, xnor_1_out, xnor_2_out, xnor_3_out, xnor_4_out);
endmodule
