// Logisim project flip_flop_d_type.circ as structural Verilog: 1 circuit, main circuit main
module main (
  input  Din,
  input  ENABLE,
  output Dout,
  output nQ,
  output Dout2
);

  wire nand_1_out, nand_2_out, not_1_out;

  not not_1 (not_1_out, Din);
  nand nand_1 (nand_1_out, Din, ENABLE);
  nand nand_2 (nand_2_out, ENABLE, not_1_out);
  D_Flip_Flop #(.trigger("high")) d_ff_1 (.D(Din), .clk(ENABLE), .Q(Dout2));  // open: Qn, preset, reset
  nand nand_3 (Dout, nand_1_out, nQ);
  nand nand_4 (nQ, Dout, nand_2_out);
endmodule
