// Logisim project flip_flop_d_type_master_slave.circ as structural Verilog: 1 circuit, main circuit main
module main (
  input  in_1,
  input  in_2,
  output out_3,
  output out_4,
  output out_5
);

  wire Master_q;

  Clock clock_1 (.out(out_3));
  D_Flip_Flop d_ff_1 (.D(in_1), .clk(in_2), .Q(out_4));  // open: Qn, preset, reset
  D_Flip_Flop #(.trigger("low")) Master (.D(in_1), .clk(in_2), .Q(Master_q));  // open: Qn, preset, reset
  D_Flip_Flop #(.trigger("high")) Slave (.D(Master_q), .clk(in_2), .Q(out_5));  // open: Qn, preset, reset
endmodule
