// Logisim project flip_flop_set_reset.circ as structural Verilog: 1 circuit, main circuit main
module main (
  input  S,
  input  R,
  output Q,
  output nQ,
  output out_5,
  output out_6,
  output out_7,
  output out_8
);

  wire button_1_out, button_2_out, button_3_out, button_4_out;

  Button #(.press("passive")) button_1 (.out(button_1_out));
  Button #(.press("passive")) button_2 (.out(button_2_out));
  Button button_3 (.out(button_3_out));
  Button button_4 (.out(button_4_out));
  nand nand_1 (Q, S, nQ);
  nand nand_2 (nQ, Q, R);
  nand nand_3 (out_5, button_1_out, out_6);
  nand nand_4 (out_6, out_5, button_2_out);
  nor nor_1 (out_7, button_3_out, out_8);
  nor nor_2 (out_8, out_7, button_4_out);
  LED led_1 (.in(out_5));
  LED led_2 (.in(out_7));
endmodule
