// Logisim project flip_flop_t_type.circ as structural Verilog: 1 circuit, main circuit main
module main (
  input  in_1,
  output out_2,
  output out_3
);

  wire d_ff_1_qn;

  D_Flip_Flop d_ff_1 (.D(d_ff_1_qn), .clk(in_1), .Q(out_2), .Qn(d_ff_1_qn));  // open: preset, reset
  T_Flip_Flop t_ff_1 (.T(1'b1), .clk(in_1), .Q(out_3));  // open: Qn, reset, preset
endmodule
