// Logisim project register_bank.circ as structural Verilog: 1 circuit, main circuit main
module main (
  input  [7:0] Din,
  input  Wr,
  input  [1:0] Reg
);

  wire decoder_1_out0, decoder_1_out1, decoder_1_out2, decoder_1_out3;

  Decoder #(.select(2)) decoder_1 (
    .out0(decoder_1_out0), .out1(decoder_1_out1), .out2(decoder_1_out2), .out3(decoder_1_out3), .sel(Reg));  // open: en
  Register #(.trigger("high")) register_1 (.D(Din), .en(Wr), .clk(decoder_1_out0));  // open: Q, clr
  Register #(.trigger("high")) register_2 (.D(Din), .en(Wr), .clk(decoder_1_out1));  // open: Q, clr
  Register #(.trigger("high")) register_3 (.D(Din), .en(Wr), .clk(decoder_1_out2));  // open: Q, clr
  Register #(.trigger("high")) register_4 (.D(Din), .en(Wr), .clk(decoder_1_out3));  // open: Q, clr
endmodule
