// Logisim project register_bank_1.circ as structural Verilog: 1 circuit, main circuit main
module main (
  input  [7:0] Din,
  input  Write,
  output [7:0] out_3,
  output [7:0] Dout
);

  Register #(.trigger("high")) register_1 (.D(Din), .clk(Write), .Q(out_3));  // open: en, clr
  D_Flip_Flop #(.trigger("high")) d_ff_1 (.D(Din[0]), .clk(Write), .Q(Dout[0]));  // open: Qn, preset, reset
  D_Flip_Flop #(.trigger("high")) d_ff_2 (.D(Din[1]), .clk(Write), .Q(Dout[1]));  // open: Qn, preset, reset
  D_Flip_Flop #(.trigger("high")) d_ff_3 (.D(Din[2]), .clk(Write), .Q(Dout[2]));  // open: Qn, preset, reset
  D_Flip_Flop #(.trigger("high")) d_ff_4 (.D(Din[3]), .clk(Write), .Q(Dout[3]));  // open: Qn, preset, reset
  D_Flip_Flop #(.trigger("high")) d_ff_5 (.D(Din[4]), .clk(Write), .Q(Dout[4]));  // open: Qn, preset, reset
  D_Flip_Flop #(.trigger("high")) d_ff_6 (.D(Din[5]), .clk(Write), .Q(Dout[5]));  // open: Qn, preset, reset
  D_Flip_Flop #(.trigger("high")) d_ff_7 (.D(Din[6]), .clk(Write), .Q(Dout[6]));  // open: Qn, preset, reset
  D_Flip_Flop #(.trigger("high")) d_ff_8 (.D(Din[7]), .clk(Write), .Q(Dout[7]));  // open: Qn, preset, reset
endmodule
