// Logisim project multiplexer_4_to_1.circ as structural Verilog: 1 circuit, main circuit main
module main (
  input  X0,
  input  X1,
  input  X2,
  input  X3,
  input  [1:0] C,
  output Y
);

  Multiplexer #(.select(2)) multiplexer_1 (.in0(X0), .in1(X1), .in2(X2), .in3(X3), .out(Y), .sel(C));
endmodule
