// Logisim project multiplexer_4_to_1_8bit.circ as structural Verilog: 1 circuit, main circuit main
module main (
  input  [7:0] X0,
  input  [7:0] X1,
  input  [7:0] X2,
  input  [7:0] X3,
  input  [1:0] C,
  output [7:0] Y
);

  Multiplexer #(.select(2), .width(8)) multiplexer_1 (.in0(X0), .in1(X1), .in2(X2), .in3(X3), .out(Y), .sel(C));
endmodule
