// Logisim project barrel_shifter_left.circ as structural Verilog: 2 circuits, main circuit main
module main (
  input  [7:0] in_bits,
  input  [1:0] num_shift,
  output [7:0] out_bits
);

  wire and_1_out, xor_1_out;
  wire [7:0] X2_out_bits;

  xor xor_1 (xor_1_out, num_shift[0], num_shift[1]);
  and and_1 (and_1_out, ~num_shift[0], num_shift[1]);  // AND_Gate
  Shifter_Left X2 (.in_bits(in_bits), .DO_SHIFT(xor_1_out), .out_bits(X2_out_bits));
  Shifter_Left X4 (.in_bits(X2_out_bits), .DO_SHIFT(and_1_out), .out_bits(out_bits));
endmodule

module Shifter_Left (
  input  [7:0] in_bits,
  input  DO_SHIFT,
  output [7:0] out_bits
);

  Multiplexer multiplexer_1 (.in0(in_bits[0]), .in1(1'b0), .out(out_bits[0]), .sel(DO_SHIFT));
  Multiplexer multiplexer_2 (.in0(in_bits[1]), .in1(in_bits[0]), .out(out_bits[1]), .sel(DO_SHIFT));
  Multiplexer multiplexer_3 (.in0(in_bits[2]), .in1(in_bits[1]), .out(out_bits[2]), .sel(DO_SHIFT));
  Multiplexer multiplexer_4 (.in0(in_bits[3]), .in1(in_bits[2]), .out(out_bits[3]), .sel(DO_SHIFT));
  Multiplexer multiplexer_5 (.in0(in_bits[4]), .in1(in_bits[3]), .out(out_bits[4]), .sel(DO_SHIFT));
  Multiplexer multiplexer_6 (.in0(in_bits[5]), .in1(in_bits[4]), .out(out_bits[5]), .sel(DO_SHIFT));
  Multiplexer multiplexer_7 (.in0(in_bits[6]), .in1(in_bits[5]), .out(out_bits[6]), .sel(DO_SHIFT));
  Multiplexer multiplexer_8 (.in0(in_bits[7]), .in1(in_bits[6]), .out(out_bits[7]), .sel(DO_SHIFT));
endmodule
