// Logisim project decoder_2bit.circ as structural Verilog: 1 circuit, main circuit main
module main (
  input  X1,
  input  X0,
  output Y0,
  output Y1,
  output Y2,
  output Y3,
  output out_7,
  output out_8,
  output out_9,
  output out_10
);

  and and_1 (Y0, ~X0, ~X1);  // AND_Gate
  and and_2 (Y1, X0, ~X1);  // AND_Gate
  and and_3 (Y2, ~X0, X1);  // AND_Gate
  and and_4 (Y3, X0, X1);
  Decoder #(.select(2)) decoder_1 (
    .out0(out_7), .out1(out_8), .out2(out_9), .out3(out_10), .sel({X1, X0}));  // open: en
endmodule
