// Logisim project encoder_2bit.circ as structural Verilog: 1 circuit, main circuit main
module main (
  input  X0,
  input  X1,
  input  X2,
  input  X3,
  output Y1,
  output Y0,
  output nVALID,
  output out_8,
  output out_9,
  output out_10
);

  wire and_1_out, and_2_out, and_3_out;

  and and_1 (and_1_out, ~X0, X1);  // AND_Gate
  and and_2 (and_2_out, ~X0, ~X1, ~X2, X3);  // AND_Gate
  and and_3 (and_3_out, ~X0, ~X1, X2);  // AND_Gate
  and and_4 (nVALID, ~X0, ~X1, ~X2, ~X3);  // AND_Gate
  Priority_Encoder #(.select(2)) priority_encoder_1 (
    .in0(X3), .in1(X2), .in2(X1), .in3(X0), .out({out_8, out_9}), .gs(out_10));  // open: en_out, en_in
  or or_1 (Y0, and_1_out, and_2_out);
  or or_2 (Y1, and_2_out, and_3_out);
endmodule
