// Logisim project simple_shifter.circ as structural Verilog: 1 circuit, main circuit main
module main (
  input  [7:0] in_bits,
  output [7:0] out_bits
);


  assign out_bits = {in_bits[6:0], 1'b0};
endmodule
