// Logisim project 4bit_counter.circ as structural Verilog: 1 circuit, main circuit main
module main (
  output [3:0] out_1,
  output b2,
  output b1,
  output b0
);

  wire clock_1_out, d_ff_1_qn, d_ff_2_qn, d_ff_3_qn, d_ff_4_qn;

  Clock clock_1 (.out(clock_1_out));
  D_Flip_Flop d_ff_1 (.D(d_ff_1_qn), .clk(clock_1_out), .Q(b0), .Qn(d_ff_1_qn));  // open: preset, reset
  D_Flip_Flop #(.trigger("falling")) d_ff_2 (.D(d_ff_2_qn), .clk(b0), .Q(b1), .Qn(d_ff_2_qn));  // open: preset, reset
  D_Flip_Flop #(.trigger("falling")) d_ff_3 (.D(d_ff_3_qn), .clk(b1), .Q(b2), .Qn(d_ff_3_qn));  // open: preset, reset
  D_Flip_Flop #(.trigger("falling")) d_ff_4 (
    .D(d_ff_4_qn), .clk(b2), .Q(out_1[3]), .Qn(d_ff_4_qn));  // open: preset, reset

  assign out_1[2:0] = {b2, b1, b0};
endmodule
