// Logisim project binary_adder.circ as structural Verilog: 3 circuits, main circuit main
module main (
  input  [3:0] X,
  input  [3:0] Y,
  output [4:0] SOMMA
);

  wire Bit_0_c1, Bit_1_cn1, Bit_2_cn1;

  Half_Adder Bit_0 (.X0(X[0]), .Y0(Y[0]), .S0(SOMMA[0]), .C1(Bit_0_c1));
  Full_Adder Bit_1 (.Cn(Bit_0_c1), .Xn(X[1]), .Yn(Y[1]), .Sn(SOMMA[1]), .Cn1(Bit_1_cn1));
  Full_Adder Bit_2 (.Cn(Bit_1_cn1), .Xn(X[2]), .Yn(Y[2]), .Sn(SOMMA[2]), .Cn1(Bit_2_cn1));
  Full_Adder BIt_3 (.Cn(Bit_2_cn1), .Xn(X[3]), .Yn(Y[3]), .Sn(SOMMA[3]), .Cn1(SOMMA[4]));
endmodule

module Half_Adder (
  input  X0,
  input  Y0,
  output S0,
  output C1
);

  wire and_1_out, and_2_out;

  and and_1 (and_1_out, ~X0, Y0);  // AND_Gate
  and and_2 (and_2_out, X0, ~Y0);  // AND_Gate
  and and_3 (C1, Y0, X0);
  or or_1 (S0, and_1_out, and_2_out);
endmodule

module Full_Adder (
  input  Cn,
  input  Xn,
  input  Yn,
  output Sn,
  output Cn1
);

  wire and_1_out, and_2_out, and_3_out, and_4_out, and_5_out, and_6_out, and_7_out;

  and and_1 (and_1_out, ~Cn, ~Xn, Yn);  // AND_Gate
  and and_2 (and_2_out, ~Cn, Xn, ~Yn);  // AND_Gate
  and and_3 (and_3_out, Cn, ~Xn, ~Yn);  // AND_Gate
  and and_4 (and_4_out, Yn, Xn, Cn);
  and and_5 (and_5_out, Xn, Yn);
  and and_6 (and_6_out, Cn, Yn);
  and and_7 (and_7_out, Cn, Xn);
  or or_1 (Sn, and_1_out, and_2_out, and_3_out, and_4_out);
  or or_2 (Cn1, and_5_out, and_6_out, and_7_out);
endmodule
