// Logisim project christmas_light_with_branch_2.circ as structural Verilog: 1 circuit, main circuit main
module main (
);

  wire clock_1_out, not_1_out;
  wire [7:0] counter_1_q, new_value, register_1_q;
  wire [8:8] rom_1_data;

  Counter counter_1 (
    .load(rom_1_data[8]), .clk(clock_1_out), .D(new_value), .Q(counter_1_q));  // open: clr, up, count, carry
  Clock clock_1 (.out(clock_1_out));
  // Probe on counter_1_q
  ROM #(.dataWidth(9)) rom_1 (.addr(counter_1_q), .data({rom_1_data[8], new_value}));
  not not_1 (not_1_out, rom_1_data[8]);
  Register #(.trigger("falling")) register_1 (
    .D(new_value), .en(not_1_out), .clk(clock_1_out), .Q(register_1_q));  // open: clr
  LED led_1 (.in(register_1_q[0]));
  LED led_2 (.in(register_1_q[1]));
  LED led_3 (.in(register_1_q[2]));
  LED led_4 (.in(register_1_q[3]));
  LED led_5 (.in(register_1_q[4]));
  LED led_6 (.in(register_1_q[5]));
  LED led_7 (.in(register_1_q[6]));
  LED led_8 (.in(register_1_q[7]));

  // Notes on the sheet:
  //   contents of rom_1 (hex, n*v repeats v):
  //   1 2 4 8 10 20 40 80 100 0 ff 109 80 40 20 10 8 4 2 1 10c f f0 115
endmodule
