// Logisim project cisc_cpu_with_microcode.circ as structural Verilog: 5 circuits, main circuit main
module main (
  input  RESET,
  input  [7:0] in_2,
  input  in_3,
  input  [7:0] IR
);

  wire A_RD, A_WR, ALU_OP, ALU_RD, CLK_out, Operand_RD, REG_RD, REG_WR, TEMP_RD, TEMP_WR;
  wire [1:0] REG_SEL;
  wire [3:0] counter_4_bit_1_count_out;
  wire [7:0] A_Reg_d_out, A_Reg_direct_out, Temp_Reg_direct_out;

  Clock CLK (.out(CLK_out));
  counter_4_bit counter_4_bit_1 (.Count_In(CLK_out), .RESET(in_3), .Count_Out(counter_4_bit_1_count_out));
  SIngleRegister A_Reg (
    .D_in(A_Reg_d_out), .CLK(CLK_out), .WR(A_WR), .RD(A_RD), .RESET(RESET), .D_out(A_Reg_d_out),
    .Direct_Out(A_Reg_direct_out));
  ROM #(.addrWidth(12), .dataWidth(11)) rom_1 (
    .addr({IR, counter_4_bit_1_count_out}),
    .data({Operand_RD, A_WR, A_RD, TEMP_WR, TEMP_RD, REG_SEL[0], REG_SEL[1], REG_WR, REG_RD, ALU_OP, ALU_RD}));
  assign A_Reg_d_out = Operand_RD ? in_2 : 8'bz;  // Controlled_Buffer controlled_buffer_1
  SIngleRegister Temp_Reg (
    .D_in(A_Reg_d_out), .CLK(CLK_out), .WR(TEMP_WR), .RD(TEMP_RD), .RESET(RESET), .D_out(A_Reg_d_out),
    .Direct_Out(Temp_Reg_direct_out));
  ALU alu_1 (.X(A_Reg_direct_out), .Operation(ALU_OP), .Y(Temp_Reg_direct_out), .RD(ALU_RD), .Res(A_Reg_d_out));
  // Probe on A_Reg_d_out
  // Probe on A_Reg_d_out
  RegisterBank registerbank_1 (
    .D_in(A_Reg_d_out), .CLK(CLK_out), .REG_SEL(REG_SEL), .WR(REG_WR), .RD(REG_RD), .RESET(RESET),
    .D_out(A_Reg_d_out));

  // Other names for the same wires on the sheet: Operand[7:0] = in_2

  // Notes on the sheet:
  //   contents of rom_1 (hex, n*v repeats v):
  //   32*0 480 201
  //   Internal Bus
endmodule

module RegisterBank (
  input  [7:0] D_in,
  input  CLK,
  input  [1:0] REG_SEL,
  input  WR,
  input  RD,
  input  RESET,
  output [7:0] D_out
);

  wire decoder_1_out0, decoder_1_out1, decoder_1_out2, decoder_1_out3;
  wire [7:0] multiplexer_1_out, R0_q, R1_q, R2_q, R3_q;

  Decoder #(.select(2)) decoder_1 (
    .out0(decoder_1_out0), .out1(decoder_1_out1), .out2(decoder_1_out2), .out3(decoder_1_out3),
    .sel(REG_SEL), .en(WR));
  Register R0 (.D(D_in), .en(decoder_1_out0), .clk(CLK), .Q(R0_q), .clr(RESET));
  Register R1 (.D(D_in), .en(decoder_1_out1), .clk(CLK), .Q(R1_q), .clr(RESET));
  Register R2 (.D(D_in), .en(decoder_1_out2), .clk(CLK), .Q(R2_q), .clr(RESET));
  Register R3 (.D(D_in), .en(decoder_1_out3), .clk(CLK), .Q(R3_q), .clr(RESET));
  Multiplexer #(.select(2), .width(8)) multiplexer_1 (
    .in0(R0_q), .in1(R1_q), .in2(R2_q), .in3(R3_q), .out(multiplexer_1_out), .sel(REG_SEL));
  assign D_out = RD ? multiplexer_1_out : 8'bz;  // Controlled_Buffer controlled_buffer_1
endmodule

module SIngleRegister (
  input  [7:0] D_in,
  input  CLK,
  input  WR,
  input  RD,
  input  RESET,
  output [7:0] D_out,
  output [7:0] Direct_Out
);

  Register register_1 (.D(D_in), .en(WR), .clk(CLK), .Q(Direct_Out), .clr(RESET));
  assign D_out = RD ? Direct_Out : 8'bz;  // Controlled_Buffer controlled_buffer_1
endmodule

module ALU (
  input  [7:0] X,
  input  Operation,
  input  [7:0] Y,
  input  RD,
  output [7:0] Res
);

  wire [7:0] adder_1_out, xor_1_out;

  xor xor_1 (xor_1_out[0], Y[0], Operation);
  xor xor_2 (xor_1_out[1], Y[1], Operation);
  xor xor_3 (xor_1_out[2], Y[2], Operation);
  xor xor_4 (xor_1_out[3], Y[3], Operation);
  xor xor_5 (xor_1_out[4], Y[4], Operation);
  xor xor_6 (xor_1_out[5], Y[5], Operation);
  xor xor_7 (xor_1_out[6], Y[6], Operation);
  xor xor_8 (xor_1_out[7], Y[7], Operation);
  Adder adder_1 (.a(X), .b(xor_1_out), .out(adder_1_out), .cin(Operation));  // open: cout
  assign Res = RD ? adder_1_out : 8'bz;  // Controlled_Buffer controlled_buffer_1
endmodule

module counter_4_bit (
  input  Count_In,
  input  RESET,
  output [3:0] Count_Out
);

  T_Flip_Flop #(.trigger("falling")) t_ff_1 (
    .T(1'b1), .clk(Count_In), .Q(Count_Out[0]), .reset(RESET));  // open: Qn, preset
  T_Flip_Flop #(.trigger("falling")) t_ff_2 (
    .T(1'b1), .clk(Count_Out[0]), .Q(Count_Out[1]), .reset(RESET));  // open: Qn, preset
  T_Flip_Flop #(.trigger("falling")) t_ff_3 (
    .T(1'b1), .clk(Count_Out[1]), .Q(Count_Out[2]), .reset(RESET));  // open: Qn, preset
  T_Flip_Flop #(.trigger("falling")) t_ff_4 (
    .T(1'b1), .clk(Count_Out[2]), .Q(Count_Out[3]), .reset(RESET));  // open: Qn, preset
endmodule
