// Logisim project flip_flop_d_falling_edge.circ as structural Verilog: 2 circuits, main circuit main
module main (
  input  D,
  input  CLOCK,
  output Q
);

  wire ff_d_level_1_1_q, not_1_out;

  not not_1 (not_1_out, CLOCK);
  FF_D_Level_1 ff_d_level_1_1 (.D(D), .CLOCK(CLOCK), .Q(ff_d_level_1_1_q));  // open: nQ
  FF_D_Level_1 ff_d_level_1_2 (.D(ff_d_level_1_1_q), .CLOCK(not_1_out), .Q(Q));  // open: nQ
endmodule

module FF_D_Level_1 (
  input  D,
  input  CLOCK,
  output Q,
  output nQ
);

  wire nand_1_out, nand_2_out, not_1_out;

  not not_1 (not_1_out, D);
  nand nand_1 (nand_1_out, D, CLOCK);
  nand nand_2 (nand_2_out, CLOCK, not_1_out);
  nand nand_3 (Q, nand_1_out, nQ);
  nand nand_4 (nQ, Q, nand_2_out);

  // Notes on the sheet:
  //   CLOCK: initial=0x1
  //   D: initial=0x1
endmodule
