// Logisim project led_sequence.circ as structural Verilog: 2 circuits, main circuit main
module main (
);

  wire and_1_out, and_2_out, and_3_out, and_4_out, and_5_out, and_6_out, and_7_out, and_8_out, clock_1_out,
       contatore_1_b0, contatore_1_b1, contatore_1_b2;

  Clock clock_1 (.out(clock_1_out));
  contatore contatore_1 (.CLK(clock_1_out), .b2(contatore_1_b2), .b1(contatore_1_b1), .b0(contatore_1_b0));
  and and_1 (and_1_out, ~contatore_1_b2, ~contatore_1_b1, ~contatore_1_b0);  // AND_Gate
  and and_2 (and_2_out, ~contatore_1_b2, contatore_1_b1, ~contatore_1_b0);  // AND_Gate
  and and_3 (and_3_out, contatore_1_b2, ~contatore_1_b1, ~contatore_1_b0);  // AND_Gate
  and and_4 (and_4_out, contatore_1_b2, contatore_1_b1, ~contatore_1_b0);  // AND_Gate
  LED led_1 (.in(and_1_out));
  and and_5 (and_5_out, ~contatore_1_b2, ~contatore_1_b1, contatore_1_b0);  // AND_Gate
  LED led_2 (.in(and_5_out));
  LED led_3 (.in(and_2_out));
  and and_6 (and_6_out, ~contatore_1_b2, contatore_1_b1, contatore_1_b0);  // AND_Gate
  LED led_4 (.in(and_6_out));
  LED led_5 (.in(and_3_out));
  and and_7 (and_7_out, contatore_1_b2, ~contatore_1_b1, contatore_1_b0);  // AND_Gate
  LED led_6 (.in(and_7_out));
  LED led_7 (.in(and_4_out));
  and and_8 (and_8_out, contatore_1_b2, contatore_1_b1, contatore_1_b0);
  LED led_8 (.in(and_8_out));
endmodule

module contatore (
  input  CLK,
  output b2,
  output b1,
  output b0
);

  T_Flip_Flop #(.trigger("falling")) t_ff_1 (.T(1'b1), .clk(CLK), .Q(b0));  // open: Qn, reset, preset
  T_Flip_Flop #(.trigger("falling")) t_ff_2 (.T(1'b1), .clk(b0), .Q(b1));  // open: Qn, reset, preset
  T_Flip_Flop #(.trigger("falling")) t_ff_3 (.T(1'b1), .clk(b1), .Q(b2));  // open: Qn, reset, preset
endmodule
