// Logisim project register_bank_2025.circ as structural Verilog: 1 circuit, main circuit main
module main (
  input  [7:0] Din,
  input  Write0,
  input  Write1,
  input  [1:0] in_4,
  input  Write2,
  input  Write3,
  output [7:0] Dout
);

  wire clock_1_out;
  wire [7:0] R0_q, R1_q, R2_q, R3_q;

  Clock clock_1 (.out(clock_1_out));
  Register #(.trigger("falling")) R0 (.D(Din), .en(Write0), .clk(clock_1_out), .Q(R0_q));  // open: clr
  Register #(.trigger("falling")) R1 (.D(Din), .en(Write1), .clk(clock_1_out), .Q(R1_q));  // open: clr
  Register #(.trigger("falling")) R2 (.D(Din), .en(Write2), .clk(clock_1_out), .Q(R2_q));  // open: clr
  Register #(.trigger("falling")) R3 (.D(Din), .en(Write3), .clk(clock_1_out), .Q(R3_q));  // open: clr
  Multiplexer #(.select(2), .width(8)) multiplexer_1 (
    .in0(R0_q), .in1(R1_q), .in2(R2_q), .in3(R3_q), .out(Dout), .sel(in_4));
endmodule
