// Logisim project sevensegment.circ as structural Verilog: 1 circuit, main circuit main
module main (
  input  [3:0] X
);

  wire undriven, undriven_2, undriven_3, undriven_4, undriven_5, undriven_6, undriven_7;

  Hex_Digit_Display hex_digit_display_1 (.value(X));  // open: dp
  ROM #(.addrWidth(4), .dataWidth(1)) SegmentA (.addr(X));  // open: data
  ROM #(.addrWidth(4), .dataWidth(1)) rom_1 (.addr(X));  // open: data
  ROM #(.addrWidth(4), .dataWidth(1)) rom_2 (.addr(X));  // open: data
  ROM #(.addrWidth(4), .dataWidth(1)) rom_3 (.addr(X));  // open: data
  ROM #(.addrWidth(4), .dataWidth(1)) rom_4 (.addr(X));  // open: data
  ROM #(.addrWidth(4), .dataWidth(1)) rom_5 (.addr(X));  // open: data
  ROM #(.addrWidth(4), .dataWidth(1)) rom_6 (.addr(X));  // open: data
  _7_Segment_Display u_7_segment_display_1 (
    .g(undriven_4), .f(undriven_3), .a(undriven), .b(undriven_2), .e(undriven_5), .d(undriven_6),
    .c(undriven_7));  // open: dp

  // Notes on the sheet:
  //   contents of SegmentA (hex, n*v repeats v):
  //   1 0 1 1 0 5*1
  //   contents of rom_1 (hex, n*v repeats v):
  //   5*1 0 0 1 1 1
  //   contents of rom_2 (hex, n*v repeats v):
  //   1 1 0 7*1
  //   contents of rom_3 (hex, n*v repeats v):
  //   1 0 1 1 0 1 1 0 1 1
  //   contents of rom_4 (hex, n*v repeats v):
  //   1 0 1 0 0 0 1 0 1
  //   contents of rom_5 (hex, n*v repeats v):
  //   1 0 0 0 1 1 1 0 1 1
  //   contents of rom_6 (hex, n*v repeats v):
  //   0 0 5*1 0 1 1
endmodule
