// Logisim project subtract.circ as structural Verilog: 1 circuit, main circuit main
module main (
  input  [7:0] X,
  input  [7:0] Y,
  output [7:0] X_minus_Y,
  output [7:0] minus_Y,
  output [7:0] out_5
);

  wire [7:0] not_1_out;

  not not_1 (not_1_out[0], Y[0]);
  not not_2 (not_1_out[1], Y[1]);
  not not_3 (not_1_out[2], Y[2]);
  not not_4 (not_1_out[3], Y[3]);
  not not_5 (not_1_out[4], Y[4]);
  not not_6 (not_1_out[5], Y[5]);
  not not_7 (not_1_out[6], Y[6]);
  not not_8 (not_1_out[7], Y[7]);
  Adder adder_1 (.a(X), .b(minus_Y), .out(X_minus_Y));  // open: cin, cout
  Adder adder_2 (.a(not_1_out), .b(8'h1), .out(minus_Y));  // open: cin, cout

  assign out_5 = minus_Y;
endmodule
