// Logisim project three_state_bus.circ as structural Verilog: 1 circuit, main circuit main
module main (
  input  [7:0] ADDR_BUS,
  input  MEM_R,
  output [7:0] DATA_BUS
);

  wire [7:0] ram_1_dout;

  RAM #(.addrWidth(7), .enables("line")) ram_1 (
    .addr(ADDR_BUS[6:0]), .din(DATA_BUS), .dout(ram_1_dout));  // open: we, clk
  RAM #(.addrWidth(7), .enables("line")) ram_2 ();  // open: addr, we, clk, din, dout
  assign DATA_BUS = MEM_R ? ram_1_dout : 8'bz;  // Controlled_Buffer controlled_buffer_1

  // Notes on the sheet:
  //   0000 0000 : 0111 1111
  //   1000 0000 : 1111 1111
endmodule
