// Logisim project tone_generator.circ as structural Verilog: 1 circuit, main circuit main
module main (
  input  Do,
  input  Re,
  input  Mi,
  input  Fa,
  input  Sol,
  input  La,
  input  Si,
  input  Do8
);

  // Buzzer buzzer_1: pin names not known; wires that end beside it: 14'h20b, Do, {7{1'b1}}
  // Buzzer buzzer_2: pin names not known; wires that end beside it: 14'h24b, Re, {7{1'b1}}
  // Buzzer buzzer_3: pin names not known; wires that end beside it: 14'h293, Mi, {7{1'b1}}
  // Buzzer buzzer_4: pin names not known; wires that end beside it: 14'h2bb, Fa, {7{1'b1}}
  // Buzzer buzzer_5: pin names not known; wires that end beside it: 14'h310, Sol, {7{1'b1}}
  // Buzzer buzzer_6: pin names not known; wires that end beside it: 14'h370, La, {7{1'b1}}
  // Buzzer buzzer_7: pin names not known; wires that end beside it: 14'h3dc, Si, {7{1'b1}}
  // Buzzer buzzer_8: pin names not known; wires that end beside it: 14'h416, Do8, {7{1'b1}}
endmodule
